# Fritzing sketch schema (saved by Fritzing 0.9.3b)
breadboards: 1

parts:
  U1 = NodeMCU V1.0
  LED1 = LED - 5mm [color="Yellow (595nm)" package="5 mm [THT]"]
  LED3 = LED - 5mm [color="Red (635nm)" package="5 mm [THT]"]
  LED4 = LED - 5mm [color="Blue (470nm)" package="5 mm [THT]"]
  LED5 = LED - 5mm [color="Green (570nm)" package="5 mm [THT]"]
  LED6 = LED - 5mm [color="Blue (470nm)" package="5 mm [THT]"]
  R1 = Resistor [tolerance=±5% resistance=220 package=THT]  # not connected
  R2 = Resistor [tolerance=±5% resistance=220 package=THT]
  R3 = Resistor [tolerance=±5% resistance=220 package=THT]
  R4 = Resistor [tolerance=±5% resistance=220 package=THT]
  R5 = Resistor [tolerance=±5% resistance=220 package=THT]

nets:
  N1: U1.D0, LED3.anode
  N2: U1.D1, LED1.anode
  N3: U1.D2, LED5.anode
  N4: U1.GND, R2.Pin_0, R3.Pin_1, R4.Pin_0, R5.Pin_0
  N5: U1.D5, LED6.anode
  N6: U1.D8, LED4.anode
  N7: LED1.cathode, R2.Pin_1
  N8: LED4.cathode, R4.Pin_1
  N9: LED5.cathode, R3.Pin_0
  N10: LED6.cathode, R5.Pin_1

custom parts:
  NodeMCU V1.0: ESP8266 based NodeMCU
